# Fritzing sketch ConexionNanoDeck (saved by Fritzing 0.9.6b)
breadboards: 1

parts:
  Componente1 = Arduino Nano (Rev3.0)
  S1 = Pushbutton [package="[SMD]"]
  S2 = Pushbutton [package="[SMD]"]
  S3 = Pushbutton [package="[SMD]"]
  S4 = Pushbutton [package="[SMD]"]
  S5 = Pushbutton [package="[SMD]"]
  S6 = Pushbutton [package="[SMD]"]
  LED1 = smd LED [color="Red (633nm)" package="0805 [SMD]"]
  LED2 = smd LED [color="Red (633nm)" package="0805 [SMD]"]
  LED3 = smd LED [color="Red (633nm)" package="0805 [SMD]"]
  LED4 = smd LED [color="Red (633nm)" package="0805 [SMD]"]
  R1 = Resistor [tolerance=±5% resistance=220 package="0402 [SMD]"]
  R2 = Resistor [tolerance=±5% resistance=220 package="0402 [SMD]"]
  R3 = Resistor [tolerance=±5% resistance=220 package="0402 [SMD]"]
  R4 = Resistor [tolerance=±5% resistance=220 package="0402 [SMD]"]
  S7 = Pushbutton [package="[SMD]"]
  S8 = Pushbutton [package="[SMD]"]

nets:
  N1: Componente1.GND, S1.Pin_1, S1.Pin_2, S2.Pin_1, S2.Pin_2, S3.Pin_1, S3.Pin_2, S4.Pin_3, S4.Pin_4, S5.Pin_3, S5.Pin_4, S6.Pin_3, S6.Pin_4, LED1.cathode, LED2.cathode, LED3.cathode, LED4.cathode, S7.Pin_1, S7.Pin_2, S8.Pin_1, S8.Pin_2
  N2: Componente1.D2, S1.Pin_3, S1.Pin_4
  N3: Componente1.D3, S2.Pin_3, S2.Pin_4
  N4: Componente1.D4, S3.Pin_3, S3.Pin_4
  N5: Componente1.D5, S4.Pin_1, S4.Pin_2
  N6: Componente1.D6, S5.Pin_1, S5.Pin_2
  N7: Componente1.D7, S6.Pin_1, S6.Pin_2
  N8: Componente1.D8, S7.Pin_3, S7.Pin_4
  N9: Componente1.D9, S8.Pin_3, S8.Pin_4
  N10: Componente1.D10, R1.Pin_1
  N11: Componente1.D11/MOSI, R2.Pin_1
  N12: Componente1.D12/MISO, R3.Pin_1
  N13: Componente1.D13/SCK, R4.Pin_1
  N14: LED1.anode, R1.Pin_0
  N15: LED2.anode, R2.Pin_0
  N16: LED3.anode, R3.Pin_0
  N17: LED4.anode, R4.Pin_0
