# Fritzing sketch Untitled Sketch (saved by Fritzing 0.9.6b)
breadboards: 1

parts:
  Componente1 = Arduino Nano (Rev3.0)
  S1 = Momentary Switch [package=ksa_sealed_tac_switch]
  S2 = Momentary Switch [package=ksa_sealed_tac_switch]
  S3 = Momentary Switch [package=ksa_sealed_tac_switch]
  S4 = Momentary Switch [package=ksa_sealed_tac_switch]
  S5 = Momentary Switch [package=ksa_sealed_tac_switch]
  S6 = Momentary Switch [package=ksa_sealed_tac_switch]
  S7 = Momentary Switch [package=ksa_sealed_tac_switch]
  S8 = Momentary Switch [package=ksa_sealed_tac_switch]
  LED1 = LED - 3mm [color="Red (633nm)" current=0.030 package="3 mm [THT]"]
  LED2 = LED - 3mm [color="Red (633nm)" current=0.030 package="3 mm [THT]"]
  LED3 = LED - 3mm [color="Red (633nm)" current=0.030 package="3 mm [THT]"]
  LED4 = LED - 3mm [color="Red (633nm)" current=0.030 package="3 mm [THT]"]
  R1 = Resistor [tolerance=±5% resistance=220 package="1206 [SMD]"]
  R2 = Resistor [tolerance=±5% resistance=220 package="1206 [SMD]"]
  R3 = Resistor [tolerance=±5% resistance=220 package="1206 [SMD]"]
  R4 = Resistor [tolerance=±5% resistance=220 package="1206 [SMD]"]

nets:
  N1: Componente1.GND, S1.3, S1.4, S2.3, S2.4, S3.3, S3.4, S4.3, S4.4, S5.3, S5.4, S6.3, S6.4, S7.3, S7.4, S8.3, S8.4, LED1.cathode, LED2.cathode, LED3.cathode, LED4.cathode
  N2: Componente1.D2, S1.1, S1.2
  N3: Componente1.D3, S2.1, S2.2
  N4: Componente1.D4, S3.1, S3.2
  N5: Componente1.D5, S4.1, S4.2
  N6: Componente1.D6, S5.1, S5.2
  N7: Componente1.D7, S6.1, S6.2
  N8: Componente1.D8, S7.1, S7.2
  N9: Componente1.D9, S8.1, S8.2
  N10: Componente1.D10, R1.Pin_1
  N11: Componente1.D11/MOSI, R2.Pin_1
  N12: Componente1.D12/MISO, R3.Pin_1
  N13: Componente1.D13/SCK, R4.Pin_1
  N14: LED1.anode, R1.Pin_0
  N15: LED2.anode, R2.Pin_0
  N16: LED3.anode, R3.Pin_0
  N17: LED4.anode, R4.Pin_0
